# Fritzing sketch AnalogTrigger (saved by Fritzing 0.9.2b)
circuit board: 5.6cm x 1.99546cm
breadboards: 1

parts:
  ZENER_5_1V = Zener Diode [part_number=1N4732A breakdown_voltage=3.6V package="300 mil [THT]"]
  R_1M = Resistor [tolerance=±5% resistance=1M package=THT]
  J1 = female pin header, 2 pins [form="♀ (female)"]
  TRIGGER = LED - 3mm [color="Red (633nm)" package="3 mm [THT]"]
  J2 = shrouded pin header, 6 pins [form="♂ (shrouded male)"]
  LED_RESISTOR = Resistor [tolerance=±5% resistance=220 package=THT]
  ZENER_5_1V1 = Zener Diode [part_number=1N4732A breakdown_voltage=3.6V package="300 mil [THT]"]
  C2 = Ceramic Capacitor [capacitance=0.1nF package="200 mil [THT, multilayer]"]
  COMP = LM 358 Dual Op-Amp [package="DIP8 [THT]"]

nets:
  N1: ZENER_5_1V.cathode, R_1M.Pin_0, J1.pin2, ZENER_5_1V1.anode, COMP.connector2
  N2: ZENER_5_1V.anode, R_1M.Pin_1, J1.pin1, J2.pin1, J2.pin2, J2.pin3, LED_RESISTOR.Pin_1, C2.0, COMP.connector3
  N3: TRIGGER.cathode, LED_RESISTOR.Pin_0
  N4: TRIGGER.anode, J2.pin4, COMP.connector0
  N5: J2.pin5, C2.1, COMP.connector1
  N6: J2.pin6, ZENER_5_1V1.cathode, COMP.connector7

notes:
  VCC
  REF
  SIG
  -
  +
  TRIGGER
  SENSOR
  BUS
  *
  GND
  1K
  101/100pF
  1N4148
  1M
  COMP
