# Fritzing sketch ArduinoBoard (saved by Fritzing 0.9.2b)
circuit board: 6.88566cm x 5.36311cm
breadboards: 2

parts:
  Arduino1 = Arduino Uno (Rev3)
  LED1 = LED - 5mm [color="Red (633nm)" package="5 mm [THT]"]
  J1 = shrouded pin header, 6 pins [form="♂ (shrouded male)"]
  R1 = Resistor [tolerance=±5% resistance=220 package=THT]

nets:
  N1: Arduino1.D9_PWM, J1.pin2
  N2: Arduino1.D10_PWM/SS, J1.pin3
  N3: Arduino1.D11_PWM/MOSI, J1.pin4
  N4: Arduino1.D12/MISO, J1.pin5
  N5: Arduino1.D13/SCK, J1.pin6
  N6: Arduino1.GND, LED1.cathode, J1.pin1
  N7: Arduino1.D7, R1.Pin_0
  N8: LED1.anode, R1.Pin_1

notes:
  You can send multiple values from the Arduino board to the computer using the serial print function. In this project, the analog values from three potentiometers are used to set the red, green, and blue values of the background color of a Processing sketch running on the computer.
  http://arduino.cc/en/Tutorial/VirtualColorMixer
  Playstation 2
  SPI Emulator
  ACK
  ATT
  COMMAND
  DATA
  CLOCK
  GND
  COMM
  CLK
  rev. 2
