# Fritzing sketch BusBoard (saved by Fritzing 0.9.2b)
circuit board: 32.3106cm x 5cm
breadboards: 1

parts:
  PI = shrouded pin header, 40 pins [form="♂ (shrouded male)"]
  J2 = shrouded pin header, 6 pins [form="♂ (shrouded male)"]
  J3 = shrouded pin header, 6 pins [form="♂ (shrouded male)"]
  J4 = shrouded pin header, 6 pins [form="♂ (shrouded male)"]
  J5 = shrouded pin header, 6 pins [form="♂ (shrouded male)"]
  J6 = shrouded pin header, 6 pins [form="♂ (shrouded male)"]
  J7 = shrouded pin header, 6 pins [form="♂ (shrouded male)"]
  J8 = shrouded pin header, 6 pins [form="♂ (shrouded male)"]
  J9 = shrouded pin header, 6 pins [form="♂ (shrouded male)"]
  J10 = shrouded pin header, 6 pins [form="♂ (shrouded male)"]
  J11 = shrouded pin header, 6 pins [form="♂ (shrouded male)"]
  J12 = shrouded pin header, 6 pins [form="♂ (shrouded male)"]
  J13 = shrouded pin header, 6 pins [form="♂ (shrouded male)"]
  J14 = shrouded pin header, 6 pins [form="♂ (shrouded male)"]
  J15 = shrouded pin header, 6 pins [form="♂ (shrouded male)"]
  J16 = shrouded pin header, 6 pins [form="♂ (shrouded male)"]
  J17 = shrouded pin header, 6 pins [form="♂ (shrouded male)"]
  GND = shrouded pin header, 6 pins [form="♂ (shrouded male)"]
  J19 = shrouded pin header, 6 pins [form="♂ (shrouded male)"]
  J21 = shrouded pin header, 6 pins [form="♂ (shrouded male)"]
  J22 = Power Jack [package=power_jack_pth_lock]
  R2 = TRIMPOT [package=3362u-2]
  J20 = shrouded pin header, 6 pins [form="♂ (shrouded male)"]
  LED1 = LED - 3mm [color="Green (570nm)" package="3 mm [THT]"]
  LED2 = LED - 3mm [color="Green (570nm)" package="3 mm [THT]"]
  LED3 = LED - 3mm [color="Green (570nm)" package="3 mm [THT]"]
  LED4 = LED - 3mm [color="Green (570nm)" package="3 mm [THT]"]
  LED5 = LED - 3mm [color="Green (570nm)" package="3 mm [THT]"]
  LED6 = LED - 3mm [color="Green (570nm)" package="3 mm [THT]"]
  LED7 = LED - 3mm [color="Green (570nm)" package="3 mm [THT]"]
  LED8 = LED - 3mm [color="Green (570nm)" package="3 mm [THT]"]
  LED9 = LED - 3mm [color="Green (570nm)" package="3 mm [THT]"]
  LED10 = LED - 3mm [color="Green (570nm)" package="3 mm [THT]"]
  LED11 = LED - 3mm [color="Green (570nm)" package="3 mm [THT]"]
  LED12 = LED - 3mm [color="Green (570nm)" package="3 mm [THT]"]
  LED13 = LED - 3mm [color="Green (570nm)" package="3 mm [THT]"]
  LED15 = LED - 3mm [color="Green (570nm)" package="3 mm [THT]"]
  LED16 = LED - 3mm [color="Green (570nm)" package="3 mm [THT]"]
  LED17 = LED - 3mm [color="Green (570nm)" package="3 mm [THT]"]
  LED18 = LED - 3mm [color="Green (570nm)" package="3 mm [THT]"]
  LED19 = LED - 3mm [color="Green (570nm)" package="3 mm [THT]"]
  LED20 = LED - 3mm [color="Green (570nm)" package="3 mm [THT]"]
  LED14 = LED - 3mm [color="Green (570nm)" package="3 mm [THT]"]
  J23 = female pin header, 2 pins [form="♀ (female)"]
  R3 = Resistor [tolerance=±5% resistance=220 package=THT]
  R4 = Resistor [tolerance=±5% resistance=220 package=THT]
  R5 = Resistor [tolerance=±5% resistance=220 package=THT]
  R6 = Resistor [tolerance=±5% resistance=220 package=THT]
  R7 = Resistor [tolerance=±5% resistance=220 package=THT]
  R8 = Resistor [tolerance=±5% resistance=220 package=THT]
  R9 = Resistor [tolerance=±5% resistance=220 package=THT]
  R10 = Resistor [tolerance=±5% resistance=220 package=THT]
  R11 = Resistor [tolerance=±5% resistance=220 package=THT]
  R12 = Resistor [tolerance=±5% resistance=220 package=THT]
  R13 = Resistor [tolerance=±5% resistance=220 package=THT]
  R14 = Resistor [tolerance=±5% resistance=220 package=THT]
  R15 = Resistor [tolerance=±5% resistance=220 package=THT]
  R16 = Resistor [tolerance=±5% resistance=220 package=THT]
  R17 = Resistor [tolerance=±5% resistance=220 package=THT]
  R18 = Resistor [tolerance=±5% resistance=220 package=THT]
  R19 = Resistor [tolerance=±5% resistance=220 package=THT]
  R20 = Resistor [tolerance=±5% resistance=220 package=THT]
  R21 = Resistor [tolerance=±5% resistance=220 package=THT]
  R22 = Resistor [tolerance=±5% resistance=220 package=THT]
  R23 = Resistor [tolerance=±5% resistance=220 package=THT]

nets:
  N1: PI.pin1, R3.Pin_1
  N2: PI.pin2, J19.pin4, LED10.anode
  N3: PI.pin3, GND.pin4, LED11.anode
  N4: PI.pin4, J15.pin4, LED12.anode
  N5: PI.pin6, J21.pin4, LED13.anode
  N6: PI.pin7, J20.pin4, LED14.anode
  N7: PI.pin8, J23.pin2, R3.Pin_0
  N8: PI.pin15, J2.pin4, LED19.anode
  N9: PI.pin16, J3.pin4, LED20.anode
  N10: PI.pin17, J4.pin4, LED18.anode
  N11: PI.pin18, J5.pin4, LED17.anode
  N12: PI.pin19, J7.pin4, LED16.anode
  N13: PI.pin21, J6.pin4, LED15.anode
  N14: PI.pin22, J8.pin4, LED6.anode
  N15: PI.pin23, J10.pin4, LED5.anode
  N16: PI.pin25, J9.pin4, LED1.anode
  N17: PI.pin30, J11.pin4, LED2.anode
  N18: PI.pin32, J14.pin4, LED3.anode
  N19: PI.pin33, J16.pin4, LED4.anode
  N20: PI.pin35, J13.pin4, LED7.anode
  N21: PI.pin36, J12.pin4, LED8.anode
  N22: PI.pin37, J17.pin4, LED9.anode
  N23: PI.pin38, J2.pin1, J3.pin1, J4.pin1, J5.pin1, J6.pin1, J7.pin1, J8.pin1, J9.pin1, J10.pin1, J11.pin1, J12.pin1, J13.pin1, J14.pin1, J15.pin1, J16.pin1, J17.pin1, GND.pin1, J19.pin1, J21.pin1, J22.GND, R2.CW, J20.pin1, J23.pin1, R4.Pin_0, R5.Pin_0, R6.Pin_0, R7.Pin_0, R8.Pin_0, R9.Pin_0, R10.Pin_0, R11.Pin_0, R12.Pin_0, R13.Pin_0, R14.Pin_0, R15.Pin_0, R16.Pin_0, R17.Pin_0, R18.Pin_0, R19.Pin_0, R20.Pin_0, R21.Pin_0, R22.Pin_0, R23.Pin_0
  N24: J2.pin2, J2.pin5, J3.pin2, J3.pin5, J4.pin2, J4.pin5, J5.pin2, J5.pin5, J6.pin2, J6.pin5, J7.pin2, J7.pin5, J8.pin2, J8.pin5, J9.pin2, J9.pin5, J10.pin2, J10.pin5, J11.pin2, J11.pin5, J12.pin2, J12.pin5, J13.pin2, J13.pin5, J14.pin2, J14.pin5, J15.pin2, J15.pin5, J16.pin2, J16.pin5, J17.pin2, J17.pin5, GND.pin2, GND.pin5, J19.pin2, J19.pin5, J21.pin2, J21.pin5, R2.WIPER, J20.pin2, J20.pin5
  N25: J2.pin6, J3.pin6, J4.pin6, J5.pin6, J6.pin6, J7.pin6, J8.pin6, J9.pin6, J10.pin6, J11.pin6, J12.pin6, J13.pin6, J14.pin6, J15.pin6, J16.pin6, J17.pin6, GND.pin6, J19.pin6, J21.pin6, J22.PWR, R2.CCW, J20.pin6
  N26: LED1.cathode, R7.Pin_1
  N27: LED2.cathode, R5.Pin_1
  N28: LED3.cathode, R6.Pin_1
  N29: LED4.cathode, R15.Pin_1
  N30: LED5.cathode, R8.Pin_1
  N31: LED6.cathode, R9.Pin_1
  N32: LED7.cathode, R23.Pin_1
  N33: LED8.cathode, R22.Pin_1
  N34: LED9.cathode, R21.Pin_1
  N35: LED10.cathode, R20.Pin_1
  N36: LED11.cathode, R19.Pin_1
  N37: LED12.cathode, R18.Pin_1
  N38: LED13.cathode, R17.Pin_1
  N39: LED15.cathode, R10.Pin_1
  N40: LED16.cathode, R11.Pin_1
  N41: LED17.cathode, R12.Pin_1
  N42: LED18.cathode, R4.Pin_1
  N43: LED19.cathode, R14.Pin_1
  N44: LED20.cathode, R13.Pin_1
  N45: LED14.cathode, R16.Pin_1

notes:
  REF
  VCC 5V
  GND
  RASPBERRY PI B+
  21
  20
  16
  12
  25
  26
  19
  13
  06
  05
  24
  23
  18
  15
  14
  UART0_RXD
  UART0_TXD
  02
  03
  GPIO 18
  04
  17
  27
  SDA1_I2C
  SCL1_I2C
  PCM_CLK
  GPIO Breakout with REF Voltage
  GPIO 22
  RESET
  PULL-UP
  rev. 2
